# Fritzing sketch drummer_schematic (saved by Fritzing 0.9.0b)
breadboards: 1

parts:
  Solenoid = Solenoid
  L3 = Solenoid
  L4 = Solenoid
  Flyback_Diode = Rectifier Diode [part_number=TIP102 package="300 mil [THT]"]
  Transistor_TIP_102 = NPN-Transistor [package="TO92 [THT]"]
  D4 = Rectifier Diode [part_number=TIP102 package="300 mil [THT]"]
  Q4 = NPN-Transistor [package="TO92 [THT]"]
  D5 = Rectifier Diode [part_number=TIP102 package="300 mil [THT]"]
  Part2 = Arduino Nano (Rev3.0)
  Q3 = NPN-Transistor [package="TO92 [THT]"]

nets:
  N1: Solenoid.pin1, Flyback_Diode.cathode, Transistor_TIP_102.C
  12V: Solenoid.pin2, L3.pin2, L4.pin2, Part2.VIN
  N2: L3.pin1, D4.cathode, Q3.C
  N3: L4.pin1, Q4.C, D5.cathode
  GND: Flyback_Diode.anode, Transistor_TIP_102.E, D4.anode, Q4.E, D5.anode, Part2.GND, Q3.E
  N4: Transistor_TIP_102.B, Part2.D10
  N5: Q4.B, Part2.D8
  N6: Part2.D9, Q3.B
